# Fritzing sketch DueUnoI2C (saved by Fritzing 0.9.2b)
breadboards: 1

parts:
  Part1 = Arduino Mega ADK (Rev3)
  Part2 = Arduino Uno (Rev3) - ICSP
  R1 = Resistor [tolerance=±5% resistance=4.7k package="2512 [SMD]"]
  R2 = Resistor [tolerance=±5% resistance=4.7k package="2512 [SMD]"]

nets:
  N1: Part1.D21/SCL, Part2.D5_PWM, R1.Pin_0
  N2: Part1.D20/SDA, Part2.D4, R2.Pin_0
  N3: Part1.5V, R1.Pin_1, R2.Pin_1
  GND: Part1.GND, Part2.GND
